// Logisim project vpu.circ as structural Verilog: 4 circuits, main circuit VPU
module VPU (
  input  in_1,
  input  [5:0] in_2,
  input  [4:0] in_3,
  input  [4:0] in_4,
  input  [31:0] in_5,
  input  [31:0] in_6,
  input  [23:0] in_7,
  output [31:0] VRegOutHi,
  output [31:0] VRegOutLo,
  output VBus32,
  output VBus64,
  output VPUError
);

  VReg VReg ();  // open: in_1, RAMOutHi, RAMOutLo
  VRegCtrl VRegCtrl ();  // open: vop, _16bitRegs, vlen, cfg

  assign VBus32 = 1'b0;
  assign VBus64 = 1'b0;
  assign VPUError = 1'b0;

  // Other names for the same wires on the sheet: CLK = in_1; RAMOutHi[31:0] = in_5; RAMOutLo[31:0] = in_6;
  //   RegOut2[23:0] = in_7; vop[5:0] = in_2; vrd[4:0] = in_3; vrs[4:0] = in_4
endmodule

module VRegRow (
  input  [31:0] RAMOutHi,
  input  [31:0] RAMOutLo,
  input  clk,
  input  [3:0] WVReg,
  output [31:0] OutHi,
  output [31:0] OutLo
);

  Register register_1 (.D(RAMOutHi[7:0]), .en(WVReg[3]), .Q(OutHi[7:0]), .clk(clk));  // open: clr
  Register register_2 (.D(RAMOutHi[15:8]), .en(WVReg[3]), .Q(OutHi[15:8]), .clk(clk));  // open: clr
  Register register_3 (.D(RAMOutHi[23:16]), .en(WVReg[2]), .Q(OutHi[23:16]), .clk(clk));  // open: clr
  Register register_4 (.D(RAMOutHi[31:24]), .en(WVReg[2]), .Q(OutHi[31:24]), .clk(clk));  // open: clr
  Register register_5 (.D(RAMOutLo[7:0]), .en(WVReg[1]), .Q(OutLo[7:0]), .clk(clk));  // open: clr
  Register register_6 (.D(RAMOutLo[15:8]), .en(WVReg[1]), .Q(OutLo[15:8]), .clk(clk));  // open: clr
  Register register_7 (.D(RAMOutLo[23:16]), .en(WVReg[0]), .Q(OutLo[23:16]), .clk(clk));  // open: clr
  Register register_8 (.D(RAMOutLo[31:24]), .en(WVReg[0]), .Q(OutLo[31:24]), .clk(clk));  // open: clr

  // Other names for the same wires on the sheet: hi[31:0] = RAMOutHi; lo[31:0] = RAMOutLo
endmodule

module VReg (
  input  in_1,
  input  [31:0] RAMOutHi,
  input  [31:0] RAMOutLo
);

  wire [31:0] vregrow_1_outhi;

  VRegRow vregrow_1 (
    .clk(in_1), .WVReg(vregrow_1_outhi[3:0]), .RAMOutHi(RAMOutHi), .RAMOutLo(RAMOutLo),
    .OutHi(vregrow_1_outhi));  // open: OutLo
  // Pins of 4 and 32 bits meet at vregrow_1_outhi

  // Other names for the same wires on the sheet: clk = in_1; RAMhi[31:0] = RAMOutHi; RAMlo[31:0] = RAMOutLo
endmodule

module VRegCtrl (
  input  [5:0] vop,
  output [3:0] _16bitRegs,
  output vlen,
  output cfg
);
endmodule
